# Fritzing sketch simple_calc (saved by Fritzing 0.8.7b)

parts:
  Part1 = LCD Display 16x2  # not connected
  LCM1602_IIC1 = LCM1602 IIC [part_number="LCM1602 IIC" chip_label="LCM1602 IIC" package="DIP (Dual Inline) [THT]"]
  Generic_4x4_button_keypad1 = Generic 4x4 Keypad
  Part2 = Arduino Uno (Rev3)

nets (from the breadboard view):
  GND: LCM1602_IIC1.GND, Part2.GND
  VCC: LCM1602_IIC1.VCC, Part2.5V
  N1: LCM1602_IIC1.SDA, Part2.A4/SDA
  N2: LCM1602_IIC1.SCL, Part2.A5/SCL
  N3: Generic_4x4_button_keypad1.C4, Part2.D9_PWM
  N4: Generic_4x4_button_keypad1.C3, Part2.D8
  N5: Generic_4x4_button_keypad1.C2, Part2.D7
  N6: Generic_4x4_button_keypad1.C1, Part2.D6_PWM
  N7: Generic_4x4_button_keypad1.R1, Part2.D5_PWM
  N8: Generic_4x4_button_keypad1.R2, Part2.D4
  N9: Generic_4x4_button_keypad1.R3, Part2.D3_PWM
  N10: Generic_4x4_button_keypad1.R4, Part2.D2

custom parts:
  LCM1602 IIC: I2C-Module to use a 1602 or 2004 LCD on with the wire.h libory Serial LCD Modul
  Generic 4x4 Keypad: generic 4x4 keypad 4 rows of four 6 mm tact switches cheap and nasty but works
